# Fritzing sketch sketch (saved by Fritzing 0.7.11b)
breadboards: 3

parts:
  Arduino1 = Arduino Mega
  IC1 = L293D [package=THT]
  M3 = DC Motor
  Power_plug1 = Power plug
  J1 = Infrared Proximity Sensor
  J2 = Infrared Proximity Sensor
  RE1 = Rotary Encoder [package=THT]
  RE2 = Rotary Encoder [package=THT]
  R1 = Rotary Potentiometer (Small) [maximum_resistance=100kΩ]
  M4 = DC Motor
  Componente1 = SRF05 Ultrasonic Rangefinder
  R2 = Photocell (LDR) [package=THT]
  R3 = Photocell (LDR) [package=THT]  # not connected
  R4 = Photocell (LDR) [package=THT]  # not connected
  R5 = Photocell (LDR) [package=THT]  # not connected
  R6 = Photocell (LDR) [package=THT]
  R7 = 10k Ω Resistor [package=THT]
  R8 = 10k Ω Resistor [package=THT]  # not connected
  R9 = 10k Ω Resistor [package=THT]

nets:
  GND: Arduino1.GND, IC1.0V, Power_plug1.GND, J1.GND, J2.GND, RE1.EncoderPinA, RE2.EncoderPinB, R1.leg2, Componente1.GND, R7.Pin_1, R9.Pin_0
  N1: Arduino1.D12, J1.Vout
  N2: Arduino1.D10, IC1.Enable_2
  N3: Arduino1.D9, IC1.Enable_1
  N4: Arduino1.D8, J2.Vout
  VCC: Arduino1.+5V, Arduino1.A10, IC1.+V, J1.Vcc, J2.Vcc, RE1.EncoderPinB, RE2.EncoderPinA, R1.leg1, R1.wiper, Componente1.VCC, R2.pin_0, R6.pin_1
  N5: Arduino1.D22, Componente1.Echo
  N6: Arduino1.D23, Componente1.Trig
  N7: Arduino1.D32, IC1.In_2
  N8: Arduino1.D33, IC1.In_1
  N9: Arduino1.D34, IC1.In_3
  N10: Arduino1.D35, IC1.In_4
  N11: Arduino1.A8, R6.pin_0, R9.Pin_1
  N12: Arduino1.A9, R2.pin_1, R7.Pin_0
  N13: Arduino1.A11, RE2.EncoderPinC
  N14: Arduino1.A12, RE1.EncoderPinC
  N15: IC1.Out_1_(_Controlled_by_Enable_1_), M4.pin_2
  N16: IC1.Out_2_(_Controlled_by_Enable_1_), M4.pin_1
  N17: IC1.+Vmotor, Power_plug1.VCC
  N18: IC1.Out_3_(_Controlled_by_Enable_2_), M3.pin_2
  N19: IC1.Out_4_(_Controlled_by_Enable_2_), M3.pin_1
